# Fritzing sketch Sketch (saved by Fritzing 0.9.3b)
breadboards: 1

parts:
  Bauteil1 = Arduino Nano (Rev3.0)
  R1 = Resistor [tolerance=±5% resistance=9k package=THT]
  R2 = Resistor [tolerance=±5% resistance=9k package=THT]
  C1 = Electrolytic Capacitor [capacitance=22µF package="100 mil [THT, electrolytic]"]
  J1 = male pin header, 2 pins [form="♂ (male)"]

nets:
  N1: Bauteil1.GND, R1.Pin_1, J1.pin1
  N2: Bauteil1.VIN, R2.Pin_1
  N3: Bauteil1.A3, R1.Pin_0, R2.Pin_0, C1.+
  N4: C1.-, J1.pin2
